// Digital circuit 5bit_adder.dig as structural Verilog
module _5bit_adder (
  input  [4:0] A,
  input  [4:0] B,
  input  Ci,
  output [4:0] S,
  output Ci_out
);

  wire full_adder_1_c_out, full_adder_2_c_out, full_adder_3_c_out, full_adder_4_c_out;

  full_adder full_adder_1 (.A(A[0]), .B(B[0]), .C_IN(Ci), .SUM(S[0]), .C_OUT(full_adder_1_c_out));
  full_adder full_adder_2 (.A(A[1]), .B(B[1]), .C_IN(full_adder_1_c_out), .SUM(S[1]), .C_OUT(full_adder_2_c_out));
  full_adder full_adder_3 (.A(A[2]), .B(B[2]), .C_IN(full_adder_2_c_out), .SUM(S[2]), .C_OUT(full_adder_3_c_out));
  full_adder full_adder_4 (.A(A[3]), .B(B[3]), .C_IN(full_adder_3_c_out), .SUM(S[3]), .C_OUT(full_adder_4_c_out));
  full_adder full_adder_5 (.A(A[4]), .B(B[4]), .C_IN(full_adder_4_c_out), .SUM(S[4]), .C_OUT(Ci_out));

  // Other names for the same wires on the sheet: Ci_in = Ci

  // Notes on the sheet:
  //   Somador_5bits
endmodule
