// Digital circuit 8bit_adder.dig as structural Verilog
module _8bit_adder (
  input  [7:0] A,
  input  [7:0] B,
  input  Ci,
  output [7:0] S,
  output CI_out
);

  wire full_adder_1_c_out, full_adder_2_c_out, full_adder_3_c_out, full_adder_4_c_out, full_adder_5_c_out,
       full_adder_6_c_out, full_adder_7_c_out;

  full_adder full_adder_1 (.A(A[0]), .B(B[0]), .C_IN(Ci), .SUM(S[0]), .C_OUT(full_adder_1_c_out));
  full_adder full_adder_2 (.A(A[1]), .B(B[1]), .C_IN(full_adder_1_c_out), .SUM(S[1]), .C_OUT(full_adder_2_c_out));
  full_adder full_adder_3 (.A(A[2]), .B(B[2]), .C_IN(full_adder_2_c_out), .SUM(S[2]), .C_OUT(full_adder_3_c_out));
  full_adder full_adder_4 (.A(A[3]), .B(B[3]), .C_IN(full_adder_3_c_out), .SUM(S[3]), .C_OUT(full_adder_4_c_out));
  full_adder full_adder_5 (.A(A[4]), .B(B[4]), .C_IN(full_adder_4_c_out), .SUM(S[4]), .C_OUT(full_adder_5_c_out));
  full_adder full_adder_6 (.A(A[5]), .B(B[5]), .C_IN(full_adder_5_c_out), .SUM(S[5]), .C_OUT(full_adder_6_c_out));
  full_adder full_adder_7 (.A(A[6]), .B(B[6]), .C_IN(full_adder_6_c_out), .SUM(S[6]), .C_OUT(full_adder_7_c_out));
  full_adder full_adder_8 (.A(A[7]), .B(B[7]), .C_IN(full_adder_7_c_out), .SUM(S[7]), .C_OUT(CI_out));

  // Other names for the same wires on the sheet: A00 = A[0]; A01 = A[1]; A02 = A[2]; A03 = A[3]; A04 = A[4];
  //   A05 = A[5]; A06 = A[6]; A07 = A[7]; B00 = B[0]; B01 = B[1]; B02 = B[2]; B03 = B[3]; B04 = B[4]; B05 = B[5];
  //   B06 = B[6]; B07 = B[7]; CI_out_t = Ci

  // Notes on the sheet:
  //   8bit adder
endmodule
