// Digital circuit 8bit_decrementor.dig as structural Verilog
module _8bit_decrementor (
  input  [7:0] A,
  output [7:0] S
);

  _8bit_adder _8bit_adder_1 (.A(A), .B({8{1'b1}}), .Ci(1'b0), .S(S));  // open: CI_out

  // Notes on the sheet:
  //   8bit decrementor
endmodule
