// Digital circuit 8bit_incrementor.dig as structural Verilog
module _8bit_incrementor (
  input  [7:0] A,
  output [7:0] S
);

  _8bit_adder _8bit_adder_1 (.A(A), .B(8'h1), .Ci(1'b0), .S(S));  // open: CI_out

  // Notes on the sheet:
  //   8bit incrementor
endmodule
