// Digital circuit 8bit_subtractor.dig as structural Verilog
module _8bit_subtractor (
  input  [7:0] A,
  input  [7:0] B,
  output [7:0] S
);

  wire [7:0] not_1_out;

  assign not_1_out = ~B;  // Not not_1, 8 bits wide
  _8bit_adder _8bit_adder_1 (.A(A), .B(not_1_out), .Ci(1'b1), .S(S));  // open: CI_out

  // Notes on the sheet:
  //   8bit subtractor
endmodule
