// Digital circuit Caminho.dig as structural Verilog
module Caminho (
  input  [7:0] WBus_in,
  input  RGA_Ld,
  input  RGB_Ld,
  input  IR_Ld,
  input  [3:0] ULA_Op,
  input  [2:0] WBus_Sel,
  input  CLK,
  input  RST,
  input  [7:0] MM_Data_in,
  input  [7:0] PC_in,
  output [7:0] WBus_Out,
  output [3:0] OpCode_Out,
  output ZF_Out
);

  wire [3:0] MM0;
  wire [7:0] MM2, Reg_A_q, Reg_B_q;

  Register #(.Bits(8)) Reg_A (.D(WBus_in), .C(CLK), .en(RGA_Ld), .Q(Reg_A_q));
  Register #(.Bits(8)) Reg_B (.D(WBus_in), .C(CLK), .en(RGB_Ld), .Q(Reg_B_q));
  ResettableRegister resettableregister_1 (.D_in(WBus_in), .CLK(CLK), .LD(IR_Ld), .RST(RST), .Q_out({OpCode_Out, MM0}));
  Multiplexer #(.Selector_Bits(3), .Bits(8)) multiplexer_1 (
    .sel(WBus_Sel), .in_0({4'b0000, MM0}), .in_1(MM_Data_in), .in_2(MM2), .in_3(Reg_A_q), .in_4(Reg_B_q),
    .in_5(PC_in), .in_6({8{1'b0}}), .in_7({8{1'b0}}), .out(WBus_Out));
  ULA ula_1 (.A_7_0(Reg_A_q), .B_7_0(Reg_B_q), .OP_3_0(ULA_Op), .Result(MM2), .FlagZero(ZF_Out));

  // Other names for the same wires on the sheet: MM1[7:0] = MM_Data_in; MM5[7:0] = PC_in; Z_flag = ZF_Out

  // Notes on the sheet:
  //   Caminhos
endmodule
