// Digital circuit ResettableRegister.dig as structural Verilog
module ResettableRegister (
  input  [7:0] D_in,
  input  CLK,
  input  LD,
  input  RST,
  output [7:0] Q_out
);

  wire [7:0] multiplexer_1_out;

  Multiplexer #(.Bits(8)) multiplexer_1 (.sel(LD), .in_0(Q_out), .in_1(D_in), .out(multiplexer_1_out));
  D_FF_AS #(.Bits(8)) d_ff_as_1 (.Set(1'b0), .D(multiplexer_1_out), .C(CLK), .Clr(RST), .Q(Q_out));  // open: nQ

  // Notes on the sheet:
  //   ResettableRegister
endmodule
