// Digital circuit ULA.dig as structural Verilog
module ULA (
  input  [7:0] A_7_0,
  input  [7:0] B_7_0,
  input  [3:0] OP_3_0,
  output [7:0] Result,
  output FlagZero
);

  wire [7:0] DEC_7_0, DIV_7_0, INC_7_0, MULT_7_0, SLB_7_0, SOMA_7_0, SUB_7_0;

  Multiplexer #(.Bits(8), .Selector_Bits(4)) multiplexer_1 (
    .sel(OP_3_0), .in_0(SOMA_7_0), .in_1(SUB_7_0), .in_2(B_7_0), .in_3(MULT_7_0), .in_4(SLB_7_0),
    .in_5(DIV_7_0), .in_6(INC_7_0), .in_7(DEC_7_0), .in_8({8{1'b0}}), .in_9({8{1'b0}}), .in_10({8{1'b0}}),
    .in_11({8{1'b0}}), .in_12({8{1'b0}}), .in_13({8{1'b0}}), .in_14({8{1'b0}}), .in_15({8{1'b0}}),
    .out(Result));
  _8bit_adder _8bit_adder_1 (.A(A_7_0), .B(B_7_0), .Ci(1'b0), .S(SOMA_7_0));  // open: CI_out
  _8bit_subtractor _8bit_subtractor_1 (.A(A_7_0), .B(B_7_0), .S(SUB_7_0));
  multiplier multiplier_1 (.A(A_7_0[3:0]), .B(B_7_0[3:0]), .Cin(1'b0), .S_mult(MULT_7_0));
  nor nor_1 (FlagZero, Result[0], Result[1], Result[2], Result[3], Result[4], Result[5], Result[6], Result[7]);
  _8bit_decrementor _8bit_decrementor_1 (.A(A_7_0), .S(DEC_7_0));
  _8bit_incrementor _8bit_incrementor_1 (.A(A_7_0), .S(INC_7_0));
  shifter_left_8bit shifter_left_8bit_1 (.A(A_7_0), .S(SLB_7_0));
  divisor divisor_1 (.A(A_7_0[3:0]), .B(B_7_0[3:0]), .Q(DIV_7_0[7:4]), .R(DIV_7_0[3:0]));

  // Other names for the same wires on the sheet: ALL_7_0[7:0] = Result

  // Notes on the sheet:
  //   ULA
endmodule
