// Digital circuit divisor.dig as structural Verilog
module divisor (
  input  [3:0] A,
  input  [3:0] B,
  output [3:0] Q,
  output [3:0] R
);

  wire [3:0] divisor_interno_1_r_out, divisor_interno_2_r_out, divisor_interno_3_r_out;

  divisor_interno divisor_interno_1 (.R_in(4'b0000), .A(A[3]), .B(B), .R_out(divisor_interno_1_r_out), .Q_out(Q[3]));
  divisor_interno divisor_interno_2 (
    .R_in(divisor_interno_1_r_out), .A(A[2]), .B(B), .R_out(divisor_interno_2_r_out), .Q_out(Q[2]));
  divisor_interno divisor_interno_3 (
    .R_in(divisor_interno_2_r_out), .A(A[1]), .B(B), .R_out(divisor_interno_3_r_out), .Q_out(Q[1]));
  divisor_interno divisor_interno_4 (.R_in(divisor_interno_3_r_out), .A(A[0]), .B(B), .R_out(R), .Q_out(Q[0]));

  // Other names for the same wires on the sheet: A00 = A[0]; A01 = A[1]; A02 = A[2]; A03 = A[3]

  // Notes on the sheet:
  //   divisor
endmodule
