// Digital circuit divisor_interno.dig as structural Verilog
module divisor_interno (
  input  [3:0] R_in,
  input  A,
  input  [3:0] B,
  output [3:0] R_out,
  output Q_out
);

  wire [3:0] M_in;
  wire [4:4] _5bit_subtrator_1_s;

  _5bit_subtrator _5bit_subtrator_1 (.A({R_in, A}), .B({1'b0, B}), .S({_5bit_subtrator_1_s[4], M_in}));
  Multiplexer #(.Bits(4)) multiplexer_1 (.sel(Q_out), .in_0({R_in[2:0], A}), .in_1(M_in), .out(R_out));
  not not_1 (Q_out, _5bit_subtrator_1_s[4]);

  // Other names for the same wires on the sheet: bp[3:0] = {R_in[2:0], A}; PartialDivisor[4:0] = {R_in, A}

  // Notes on the sheet:
  //   Divisor-Interno
endmodule
