// Digital circuit full_adder.dig as structural Verilog
module full_adder (
  input  A,
  input  B,
  input  C_IN,
  output SUM,
  output C_OUT
);

  wire half_adder_1_carry, half_adder_1_sum, half_adder_2_carry;

  half_adder half_adder_1 (.A(A), .B(B), .SUM(half_adder_1_sum), .Carry(half_adder_1_carry));
  half_adder half_adder_2 (.A(C_IN), .B(half_adder_1_sum), .SUM(SUM), .Carry(half_adder_2_carry));
  or or_1 (C_OUT, half_adder_1_carry, half_adder_2_carry);

  // Notes on the sheet:
  //   Full Adder
endmodule
