// Digital circuit half_adder.dig as structural Verilog
module half_adder (
  input  A,
  input  B,
  output SUM,
  output Carry
);

  xor xor_1 (SUM, A, B);
  and and_1 (Carry, A, B);

  // Notes on the sheet:
  //   Half Adder
endmodule
