// Digital circuit main_cpu.dig as structural Verilog
module main_cpu (
  input  CLK,
  input  RST
);

  wire caminho_1_zf_out, controle_1_out_ld, CPU_CLK, HLT, IR_ld, MAR_ld, not_1_out, PC_en, PC_ld, RegA_ld,
       RegB_ld;
  wire [2:0] WBus_sel;
  wire [3:0] caminho_1_opcode_out, ULA_op;
  wire [7:0] caminho_1_wbus_out, memoria_1_data_out, resettableregister_1_q_out, undriven;

  memoria memoria_1 (.WBI(caminho_1_wbus_out), .MAR(MAR_ld), .CLK(CPU_CLK), .RST(RST), .Data_Out(memoria_1_data_out));
  PC pc_1 ();
  Caminho caminho_1 (
    .WBus_in(caminho_1_wbus_out), .RGA_Ld(RegA_ld), .RGB_Ld(RegB_ld), .IR_Ld(IR_ld), .ULA_Op(ULA_op),
    .WBus_Sel(WBus_sel), .CLK(CPU_CLK), .RST(RST), .MM_Data_in(memoria_1_data_out), .PC_in(undriven),
    .WBus_Out(caminho_1_wbus_out), .OpCode_Out(caminho_1_opcode_out), .ZF_Out(caminho_1_zf_out));
  not not_1 (not_1_out, HLT);
  controle controle_1 (
    .i_OpCode(caminho_1_opcode_out), .i_ZF(caminho_1_zf_out), .CLK(CPU_CLK), .RST(RST), .WBus_Sel(WBus_sel),
    .PC_en(PC_en), .PC_ld(PC_ld), .MAR_ld(MAR_ld), .IR_ld(IR_ld), .RegA_ld(RegA_ld), .RegB_ld(RegB_ld),
    .OUT_ld(controle_1_out_ld), .ULA_op(ULA_op), .HLT(HLT));
  and and_1 (CPU_CLK, not_1_out, CLK);
  ResettableRegister resettableregister_1 (
    .D_in(caminho_1_wbus_out), .CLK(CPU_CLK), .LD(controle_1_out_ld), .RST(RST),
    .Q_out(resettableregister_1_q_out));
  Seven_Seg_Hex seven_seg_hex_1 (.d(resettableregister_1_q_out[7:4]), .dp(1'b0));
  Seven_Seg_Hex seven_seg_hex_2 (.d(resettableregister_1_q_out[3:0]), .dp(1'b0));

  // Notes on the sheet:
  //   CLK: Hz: 3
  //   MAIN
endmodule
