// Digital circuit multiplier.dig as structural Verilog
module multiplier (
  input  [3:0] A,
  input  [3:0] B,
  input  Cin,
  output [7:0] S_mult
);

  wire P00, P01, P02, P03, P04, P05, P06, P07, P08, P09, P10, P11, P12, P13, P14, P15;
  wire [7:0] _8bit_adder_1_s, _8bit_adder_2_s;

  and and_1 (P00, A[0], B[0]);
  and and_2 (P04, A[0], B[1]);
  and and_3 (P08, A[0], B[2]);
  and and_4 (P12, A[0], B[3]);
  _8bit_adder _8bit_adder_1 (
    .A({4'b0000, P03, P02, P01, P00}), .B({3'b000, P07, P06, P05, P04, 1'b0}), .Ci(Cin), .S(_8bit_adder_1_s));  // open: CI_out
  _8bit_adder _8bit_adder_2 (
    .A({2'b00, P11, P10, P09, P08, 2'b00}), .B({1'b0, P15, P14, P13, P12, 3'b000}), .Ci(Cin),
    .S(_8bit_adder_2_s));  // open: CI_out
  and and_5 (P01, A[1], B[0]);
  and and_6 (P05, A[1], B[1]);
  and and_7 (P09, A[1], B[2]);
  and and_8 (P13, A[1], B[3]);
  _8bit_adder _8bit_adder_3 (.A(_8bit_adder_1_s), .B(_8bit_adder_2_s), .Ci(Cin), .S(S_mult));  // open: CI_out
  and and_9 (P02, A[2], B[0]);
  and and_10 (P06, A[2], B[1]);
  and and_11 (P10, A[2], B[2]);
  and and_12 (P14, A[2], B[3]);
  and and_13 (P03, A[3], B[0]);
  and and_14 (P07, A[3], B[1]);
  and and_15 (P11, A[3], B[2]);
  and and_16 (P15, A[3], B[3]);

  // Notes on the sheet:
  //   multiplier
endmodule
