// Digital circuit shifter_left_8bit.dig as structural Verilog
module shifter_left_8bit (
  input  [7:0] A,
  output [7:0] S
);


  assign S = {A[6:0], 1'b0};

  // Notes on the sheet:
  //   shifter_left_8bit
endmodule
